# Fritzing sketch wiring diagram (saved by Fritzing 0.9.9b)

parts:
  Ac_Power = Power plug
  Mod1 = Raspberry Pi Pico
  M1 = RioRand LM2596
  HLK-PM3 = HLK-PM12 [part_number=HLK-PM12]
  M2 = DC Motor
  M3 = DC Motor
  M4 = DC Motor
  M5 = DC Motor
  M6 = DC Motor
  M7 = DC Motor
  M8 = DC Motor
  M9 = DC Motor
  M10 = DC Motor
  M11 = DC Motor
  M12 = DC Motor
  M13 = DC Motor
  M14 = DC Motor
  M17 = DC Motor
  M15 = DC Motor
  M16 = DC Motor
  HLK-PM4 = HLK-PM01
  Ac_Power1 = Power plug
  Mod2 = Raspberry Pi 4B  # not connected
  Mod3 = Raspberry Pi Pico
  Part17 = IFR520 MOS module [package=THT]
  M18 = DC Motor
  L1 = Solenoid
  L2 = Solenoid
  L3 = Solenoid
  L4 = Solenoid
  R1 = Heating Pad
  R2 = Heating Pad
  YF-S201_Flow_Meter1 = YF-S201 Water Flow Meter
  YF-S201_Flow_Meter2 = YF-S201 Water Flow Meter
  Water_Level_Sensor1 = Water Level Sensor
  Water_Level_Sensor2 = Water Level Sensor
  Part18 = Humidity Sensor - HIH-4030 Breakout
  Part19 = Humidity Sensor - HIH-4030 Breakout
  Water_Level_Sensor3 = Water Level Sensor
  U1 = TEMPERATURE-SENSOR [package=to-92]
  U2 = TEMPERATURE-SENSOR [package=to-92]
  EC-Salinity_Probe_Interface2 = EC-Salinity Probe Interface [chip_label="EC-Salinity Probe Interface" package="DIP (Dual Inline) [THT]"]
  S1 = PH meter [package=THT]
  Grove1 = Grove Light Sensor
  Grove2 = Grove Light Sensor
  LED1 = LEDs [package=led10mm]
  LED2 = LEDs [package=led10mm]
  M19 = DC Motor
  8_Channel_Relay3 = 8 Channel Power Relay
  8_Channel_Relay4 = 8 Channel Power Relay
  Part21 = IFR520 MOS module [package=THT]
  Part22 = IFR520 MOS module [package=THT]
  Part23 = IFR520 MOS module [package=THT]
  Part24 = IFR520 MOS module [package=THT]
  8_Channel_Relay5 = 8 Channel Power Relay
  Part25 = IFR520 MOS module [package=THT]
  Part26 = IFR520 MOS module [package=THT]

nets:
  N1: Ac_Power.VCC, HLK-PM3.AC_1
  N2: Ac_Power.GND, HLK-PM3.AC_2
  N3: Mod1.pin_1, 8_Channel_Relay3.IN1
  N4: Mod1.pin_2, 8_Channel_Relay3.IN2
  GND: Mod1.pin_3, Mod1.pin_8, Mod1.pin_13, Mod1.pin_18, Mod1.pin_23, Mod1.pin_42, HLK-PM4.-Vo, Part17.GND, M18.pin_1, YF-S201_Flow_Meter1.GND, YF-S201_Flow_Meter2.GND, Water_Level_Sensor1.GND, Water_Level_Sensor2.GND, Part18.GND, Part19.GND, Water_Level_Sensor3.GND, U1.GND, U2.GND, EC-Salinity_Probe_Interface2.GND, S1.pin3, Grove1.GND, Grove2.GND, 8_Channel_Relay3.GND, 8_Channel_Relay4.GND, Part21.GND, Part22.GND, Part23.GND, Part24.GND, 8_Channel_Relay5.GND, Part25.GND, Part26.GND
  N5: Mod1.pin_4, 8_Channel_Relay3.IN3
  N6: Mod1.pin_5, 8_Channel_Relay3.IN4
  N7: Mod1.pin_6, 8_Channel_Relay3.IN5
  N8: Mod1.pin_7, 8_Channel_Relay3.IN6
  N9: Mod1.pin_9, 8_Channel_Relay3.IN7
  N10: Mod1.pin_10, 8_Channel_Relay3.IN8
  N11: Mod1.pin_11, 8_Channel_Relay4.IN1
  N12: Mod1.pin_12, 8_Channel_Relay4.IN2
  N13: Mod1.pin_14, 8_Channel_Relay4.IN3
  N14: Mod1.pin_15, 8_Channel_Relay4.IN4
  N15: Mod1.pin_16, 8_Channel_Relay4.IN5
  N16: Mod1.pin_17, 8_Channel_Relay4.IN6
  N17: Mod1.pin_19, 8_Channel_Relay4.IN7
  N18: Mod1.pin_20, 8_Channel_Relay4.IN8
  N19: Mod1.pin_21, Part17.SIG
  N20: Mod1.pin_22, Part21.SIG
  N21: Mod1.pin_24, Part22.SIG
  N22: Mod1.pin_25, Part23.SIG
  N23: Mod1.pin_26, Part24.SIG
  N24: Mod1.pin_27, 8_Channel_Relay5.IN1
  N25: Mod1.pin_29, 8_Channel_Relay5.IN2
  N26: Mod1.pin_31, 8_Channel_Relay5.IN3
  N27: Mod1.pin_32, Part25.SIG
  N28: Mod1.pin_34, Part26.SIG
  VCC: Mod1.pin_36, Part17.VCC, Part21.VCC, Part22.VCC, Part23.VCC, Part24.VCC, Part25.VCC, Part26.VCC
  N29: M1.Pin_1, HLK-PM3.+Vo
  N30: M1.Pin_2, HLK-PM3.-Vo
  N31: M1.Pin_3, Part17.V+, 8_Channel_Relay3.NO, 8_Channel_Relay4.NO
  N32: M1.Pin_4, M2.pin_2, M3.pin_2, M4.pin_2, M5.pin_2, M6.pin_2, M7.pin_2, M8.pin_2, M9.pin_2, M10.pin_2, M11.pin_2, M12.pin_2, M13.pin_2, M14.pin_2, M17.pin_2, M15.pin_2, M16.pin_2, Part17.V-
  N33: M2.pin_1, 8_Channel_Relay3.COM#34
  N34: M3.pin_1, 8_Channel_Relay3.COM#37
  N35: M4.pin_1, 8_Channel_Relay3.COM#40
  N36: M5.pin_1, 8_Channel_Relay3.COM#43
  N37: M6.pin_1, 8_Channel_Relay3.COM#22
  N38: M7.pin_1, 8_Channel_Relay3.COM#25
  N39: M8.pin_1, 8_Channel_Relay3.COM#28
  N40: M9.pin_1, 8_Channel_Relay3.COM#31
  N41: M10.pin_1, 8_Channel_Relay4.COM#40
  N42: M11.pin_1, 8_Channel_Relay4.COM#43
  N43: M12.pin_1, 8_Channel_Relay4.COM#34
  N44: M13.pin_1, 8_Channel_Relay4.COM#37
  N45: M14.pin_1, 8_Channel_Relay4.COM#31
  N46: M17.pin_1, 8_Channel_Relay4.NC
  N47: M15.pin_1, 8_Channel_Relay4.COM#25
  N48: M16.pin_1, 8_Channel_Relay4.COM#28
  N49: HLK-PM4.AC#0, Ac_Power1.VCC, 8_Channel_Relay5.NO
  N50: HLK-PM4.AC#1, Ac_Power1.GND, LED1.A, LED1.C, LED2.A, M19.pin_1, 8_Channel_Relay5.COM#28
  VCC_2: HLK-PM4.+Vo, YF-S201_Flow_Meter1.VCC, YF-S201_Flow_Meter2.VCC, Water_Level_Sensor1.VCC, Water_Level_Sensor2.VCC, Part18.VCC, Part19.VCC, Water_Level_Sensor3.VCC, U1.VCC, U2.VCC, EC-Salinity_Probe_Interface2.VCC, S1.pin2, Grove1.VCC, Grove2.VCC, 8_Channel_Relay3.VCC#17, 8_Channel_Relay4.VCC#17, Part21.VIN, Part22.VIN, Part23.VIN, Part24.VIN, 8_Channel_Relay5.VCC#17, Part25.VIN, Part26.VIN
  N51: Mod3.pin_1, YF-S201_Flow_Meter2.SIG
  N52: Mod3.pin_2, YF-S201_Flow_Meter1.SIG
  N53: Mod3.pin_4, Water_Level_Sensor2.SIG
  N54: Mod3.pin_5, Water_Level_Sensor1.SIG
  N55: Mod3.pin_6, Water_Level_Sensor3.SIG
  N56: Mod3.pin_7, Part18.OUT
  N57: Mod3.pin_9, Part19.OUT
  N58: Mod3.pin_10, U1.ADJ
  N59: Mod3.pin_11, U2.ADJ
  N60: Mod3.pin_12, S1.pin1
  N61: Mod3.pin_14, EC-Salinity_Probe_Interface2.SDA
  N62: Mod3.pin_15, Grove1.SIG
  N63: Mod3.pin_16, Grove2.SIG
  N64: Part17.VIN, M18.pin_2
  N65: L1.pin1, Part24.V-
  N66: L1.pin2, Part24.V+
  N67: L2.pin1, Part23.V-
  N68: L2.pin2, Part23.V+
  N69: L3.pin1, Part22.V-
  N70: L3.pin2, Part22.V+
  N71: L4.pin1, Part21.V-
  N72: L4.pin2, Part21.V+
  N73: R1.pin_0, Part25.V+
  N74: R1.pin_1, Part25.V-
  N75: R2.pin_0, Part26.V+
  N76: R2.pin_1, Part26.V-
  N77: LED2.C, 8_Channel_Relay5.COM#25
  N78: M19.pin_2, 8_Channel_Relay5.COM#22
  N79: 8_Channel_Relay3.VCC#19, 8_Channel_Relay3.JD-VCC
  N80: 8_Channel_Relay4.VCC#19, 8_Channel_Relay4.JD-VCC
  N81: 8_Channel_Relay5.VCC#19, 8_Channel_Relay5.JD-VCC

notes:
  Ac Power
  OUTPUT : 24VDC
  Peristalic Pumps
  IN : 24v | OUT : 12v
  water pump
  Pico 1 : control
  Pico 2 : sensors
  Solenoid 3
  Heating pad bin 1
  Heating pad bin 2
  5v Relay switch
  Water Sensors
  Hall Effect Sensor
  Solenoid 1
  Solenoid 2
  Solenoid 4
  Temperature sensors
  Airstone pump
  5v Relay switch (4 channel)
  Mosfets

custom parts:
  Raspberry Pi Pico: Raspberry Pi Pico. Based around the RP2040 microcontroller the Pico is a low cost microcontroller device bringing Raspberry Pi quality, cost, and easy of use to the microcontroller space. Jan 2021, Split part in to two versions: tht (this one) and SMD. This one will drill holes for a .1 in header in pcb to allow plugging in the module as well as providing pads to solder the module to the top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
  Heating Pad: A thermoresistant material with an embeded conductor that dissipates electrical energy into heat.
  YF-S201 Water Flow Meter: The YF-S201 Flow Meter. The input voltage is 5V to 24V (DC).
  Water Level Sensor: A water level sensor. This sensor operates at 3V to 5V. The Sig (signal) pin outputs an analogue signal that is in proportion to the amount of water in contact with the sensor.
  LEDs: LEDs Standard schematic elements and footprints for 5mm, 3mm, 1206, and 0603 sized LEDs. 5mm - Spark Fun Electronics SKU : COM-00529 (and others)
  8 Channel Power Relay: An 8 channel power relay. The module operates at 5V.
